// Logisim project M3_Gerador_de_Sequência.circ as structural Verilog: 4 circuits, main circuit Gerador_de_Sequência
module Sequencia_Henry (
  input  Clear,
  input  Clock,
  input  Preset,
  output \Último_número_da_sequência ,
  output Q3,
  output Q2,
  output Q1,
  output Q0
);

  wire A_qn, and_1_out, and_2_out, and_3_out, and_4_out, and_6_out, and_7_out, and_8_out, and_9_out,
       and_10_out, and_11_out, and_12_out, and_13_out, and_14_out, and_15_out, and_16_out, and_17_out, B_qn,
       C_qn, D_qn, or_1_out, or_2_out, or_3_out, or_4_out;

  or or_1 (or_1_out, and_1_out, and_2_out, and_3_out, and_4_out);
  and and_1 (and_1_out, A_qn, C_qn);
  and and_2 (and_2_out, B_qn, C_qn);
  and and_3 (and_3_out, C_qn, D_qn);
  and and_4 (and_4_out, Q1, Q0);
  D_Flip_Flop A (.clk(Clock), .D(or_1_out), .Q(Q3), .Qn(A_qn), .preset(Preset), .en(1'b1), .reset(Clear));
  or or_2 (or_2_out, and_6_out, and_7_out, and_8_out, and_9_out);
  and and_5 (\Último_número_da_sequência , Q3, B_qn, C_qn, D_qn);
  D_Flip_Flop B (.clk(Clock), .D(or_2_out), .Q(Q2), .Qn(B_qn), .preset(Preset), .en(1'b1), .reset(Clear));
  and and_6 (and_6_out, C_qn, D_qn);
  and and_7 (and_7_out, Q2, Q0);
  and and_8 (and_8_out, Q2, Q3);
  and and_9 (and_9_out, Q3, Q1, Q0);
  or or_3 (or_3_out, and_10_out, and_11_out, and_12_out);
  Hex_Digit_Display hex_digit_display_1 (.value({Q3, Q2, Q1, Q0}));  // open: dp
  and and_10 (and_10_out, A_qn, Q2, Q1);
  and and_11 (and_11_out, Q3, C_qn, Q0);
  and and_12 (and_12_out, Q3, Q1, D_qn);
  D_Flip_Flop C (.clk(Clock), .D(or_3_out), .Q(Q1), .Qn(C_qn), .preset(Preset), .en(1'b1), .reset(Clear));
  or or_4 (or_4_out, and_13_out, and_14_out, and_15_out, and_16_out, and_17_out);
  and and_13 (and_13_out, A_qn, D_qn);
  and and_14 (and_14_out, C_qn, D_qn);
  and and_15 (and_15_out, Q2, C_qn);
  and and_16 (and_16_out, A_qn, B_qn, Q1);
  and and_17 (and_17_out, Q3, Q1, Q0);
  D_Flip_Flop D (.clk(Clock), .D(or_4_out), .Q(Q0), .Qn(D_qn), .preset(Preset), .en(1'b1), .reset(Clear));

  // Notes on the sheet:
  //   Q3
  //   Q2
  //   Q1
  //   Q0
endmodule

module Suquencia_Extra (
  input  Clear,
  input  Clock,
  input  Preset,
  output \Último_número_da_sequência ,
  output Q3,
  output Q2,
  output Q1,
  output Q0
);

  wire A_qn, and_1_out, and_2_out, and_3_out, and_4_out, and_5_out, and_6_out, and_8_out, and_9_out,
       and_10_out, and_11_out, and_12_out, and_13_out, B_qn, C_qn, D_qn, or_1_out, or_2_out, or_3_out,
       or_4_out;

  or or_1 (or_1_out, and_1_out, and_2_out);
  and and_1 (and_1_out, Q2, Q0);
  and and_2 (and_2_out, A_qn, Q1, Q0);
  D_Flip_Flop A (.clk(Clock), .D(or_1_out), .Q(Q3), .Qn(A_qn), .preset(Preset), .en(1'b1), .reset(Clear));
  or or_2 (or_2_out, and_3_out, and_4_out, and_5_out, and_6_out);
  and and_3 (and_3_out, A_qn, Q1, Q0);
  and and_4 (and_4_out, Q3, Q2, Q1);
  and and_5 (and_5_out, A_qn, Q2, C_qn, D_qn);
  and and_6 (and_6_out, Q3, B_qn, C_qn, Q0);
  and and_7 (\Último_número_da_sequência , Q3, B_qn, Q1, D_qn);
  D_Flip_Flop B (.clk(Clock), .D(or_2_out), .Q(Q2), .Qn(B_qn), .preset(Preset), .en(1'b1), .reset(Clear));
  or or_3 (or_3_out, and_8_out, and_9_out);
  Hex_Digit_Display hex_digit_display_1 (.value({Q3, Q2, Q1, Q0}));  // open: dp
  D_Flip_Flop C (.clk(Clock), .D(or_3_out), .Q(Q1), .Qn(C_qn), .preset(Preset), .en(1'b1), .reset(Clear));
  and and_8 (and_8_out, A_qn, Q0);
  and and_9 (and_9_out, Q3, Q2, Q1, D_qn);
  or or_4 (or_4_out, D_qn, and_10_out, and_11_out, and_12_out, and_13_out);
  and and_10 (and_10_out, Q2, Q1);
  and and_11 (and_11_out, Q3, Q1);
  and and_12 (and_12_out, Q3, Q2);
  and and_13 (and_13_out, A_qn, B_qn, C_qn);
  D_Flip_Flop D (.clk(Clock), .D(or_4_out), .Q(Q0), .Qn(D_qn), .preset(Preset), .en(1'b1), .reset(Clear));

  // Notes on the sheet:
  //   Q3
  //   Q2
  //   Q1
  //   Q0
endmodule

module \Gerador_de_Sequência  (
  input  in_1,
  input  in_2,
  input  in_3,
  output [3:0] out_4
);

  wire or_1_out, \sequencia_henry_1_último_número_da_sequência ,
       \suquencia_extra_1_último_número_da_sequência , t_ff_1_q;
  wire [3:0] sequencia_henry_1_q0, suquencia_extra_1_q0;

  Hex_Digit_Display hex_digit_display_1 (.value(sequencia_henry_1_q0));  // open: dp
  Sequencia_Henry sequencia_henry_1 (
    .Clock(in_1), .Q3(sequencia_henry_1_q0[3]), .Q2(sequencia_henry_1_q0[2]), .Q1(sequencia_henry_1_q0[1]),
    .Q0(sequencia_henry_1_q0[0]), .Preset(in_3), .Clear(in_2),
    .\Último_número_da_sequência (\sequencia_henry_1_último_número_da_sequência ));
  Hex_Digit_Display hex_digit_display_2 (.value(out_4));  // open: dp
  Multiplexer #(.width(4), .enable("false")) multiplexer_1 (
    .in0(sequencia_henry_1_q0), .in1(suquencia_extra_1_q0), .out(out_4), .sel(t_ff_1_q));
  Hex_Digit_Display hex_digit_display_3 (.value(suquencia_extra_1_q0));  // open: dp
  or or_1 (or_1_out, \suquencia_extra_1_último_número_da_sequência , \sequencia_henry_1_último_número_da_sequência );
  Suquencia_Extra suquencia_extra_1 (
    .Clock(in_1), .Q3(suquencia_extra_1_q0[3]), .Q2(suquencia_extra_1_q0[2]), .Q1(suquencia_extra_1_q0[1]),
    .Q0(suquencia_extra_1_q0[0]), .Preset(in_3), .Clear(in_2),
    .\Último_número_da_sequência (\suquencia_extra_1_último_número_da_sequência ));
  T_Flip_Flop t_ff_1 (.clk(in_1), .T(or_1_out), .Q(t_ff_1_q));  // open: Qn, preset, reset, en

  // Notes on the sheet:
  //   Sequência Henry: 13 - 7 - 14 - 6 - 3 - 9 - 10 -2 - 1 - 8
  //   Sequência Extra: 1 - 3 - 14 - 7 - 15 - 13 - 9 - 4 - 5 - 10
endmodule

module Circuito_Final (
  input  Ck,
  input  Preset,
  input  Clear
);

  wire [3:0] \gerador_de_sequência_1_out_4 ;

  Hex_Digit_Display hex_digit_display_1 (.value(\gerador_de_sequência_1_out_4 ));  // open: dp
  \Gerador_de_Sequência  \gerador_de_sequência_1  (
    .in_1(Ck), .in_2(Clear), .out_4(\gerador_de_sequência_1_out_4 ), .in_3(Preset));

  // Notes on the sheet:
  //   Sequência Henry: 13 - 7 - 14 - 6 - 3 - 9 - 10 -2 - 1 - 8
  //   Sequência Extra: 1 - 3 - 14 - 7 - 15 - 13 - 9 - 4 - 5 - 10
endmodule
